// Logisim project demultiplexer_impl.circ as structural Verilog: 1 circuit, main circuit main
module main (
  input  S1,
  input  S0,
  input  D,
  output R3,
  output R2,
  output R1,
  output R0
);

  wire not_1_out, not_2_out;

  not not_1 (not_1_out, S1);
  not not_2 (not_2_out, S0);
  and and_1 (R3, S1, S0, D);
  and and_2 (R2, S1, not_2_out, D);
  and and_3 (R1, not_1_out, S0, D);
  and and_4 (R0, not_1_out, not_2_out, D);
endmodule
