// Logisim project full_subtractor.circ as structural Verilog: 1 circuit, main circuit main
module main (
  input  A,
  input  B,
  input  Borrow_in,
  output Result,
  output Borrow_out
);

  wire and_1_out, and_2_out, and_3_out, and_4_out, not_1_out, not_2_out, not_3_out;

  not not_1 (not_1_out, A);
  not not_2 (not_2_out, B);
  not not_3 (not_3_out, Borrow_in);
  and and_1 (and_1_out, A, B, Borrow_in);
  and and_2 (and_2_out, A, not_2_out, not_3_out);
  and and_3 (and_3_out, not_1_out, B, not_3_out);
  and and_4 (and_4_out, not_1_out, not_2_out, Borrow_in);
  or or_1 (Result, and_1_out, and_2_out, and_3_out, and_4_out);
  or or_2 (Borrow_out, and_1_out, and_3_out, and_4_out);
endmodule
