// Logisim project half_adder.circ as structural Verilog: 1 circuit, main circuit main
module main (
  input  A,
  input  B,
  output Result,
  output Carry
);

  and and_1 (Carry, A, B);
  xor xor_1 (Result, A, B);
endmodule
