// Logisim project half_subtractor.circ as structural Verilog: 1 circuit, main circuit main
module main (
  input  A,
  input  B,
  output Result,
  output Borrow_out
);

  wire not_1_out;

  not not_1 (not_1_out, A);
  xor xor_1 (Result, A, B);
  and and_1 (Borrow_out, not_1_out, B);
endmodule
