// Logisim project xor.circ as structural Verilog: 2 circuits, main circuit pdnf_xor
module pdnf_xor (
  input  A,
  input  B,
  output Result
);

  wire not_1_out, not_2_out, or_1_out, or_2_out;

  not not_1 (not_1_out, A);
  not not_2 (not_2_out, B);
  or or_1 (or_1_out, A, B);
  or or_2 (or_2_out, not_1_out, not_2_out);
  and and_1 (Result, or_1_out, or_2_out);
endmodule

module pcnf_xor (
  input  A,
  input  B,
  output Result
);

  wire and_1_out, and_2_out, not_1_out, not_2_out;

  not not_1 (not_1_out, A);
  not not_2 (not_2_out, B);
  and and_1 (and_1_out, A, not_2_out);
  and and_2 (and_2_out, not_1_out, B);
  or or_1 (Result, and_1_out, and_2_out);
endmodule
